# Fritzing sketch radiohead-relay-power (saved by Fritzing 1.0.8)

parts:
  R1 = R1 / 100k
  R2 = R2 / 100k
  R3 = R3 / 10k
  R4 = R4 / 100k
  R5 = R5 / 1k
  R6 = R6 / 100k
  R7 = R7 / 1k
  R8 = R8 / 47k
  R9 = R9 / 10k
  R10 = R10 / 22k
  R11 = R11 / 100k
  R12 = R12 / 47k
  R13 = R13 / 100k
  R14 = R14 / 10k
  R15 = R15 / 100k
  C1 = C1 / 100nF
  C2 = C2 / 1uF
  C3 = C3 / 10nF
  C4 = C4 / 470uF 16V
  D1 = D1 / 1N4148
  D2 = D2 / 1N4148
  Q1 = Q1 / 2N3904
  Q2 = Q2 / 2N3904
  Q3 = Q3 / 2N3906
  Q4 = Q4 / 2N3904
  Q5 = Q5 / 2N3904
  U1 = U1 / SN74HC132N
  SW1 = SW1 / encoder momentary
  PROTECT = PROTECT / 1S >=6A; exact board to verify
  F1 = F1 / 5A time-delay provisional
  CELL1 = CELL1 / matched 18650
  CELL2 = CELL2 / matched 18650
  RELAY = RELAY / existing Songle module
  IP5310 = IP5310 / USB-C + USB-A
  ESP32 = ESP32 / existing dev board
  MAX_LEFT = MAX_LEFT / MAX98357
  MAX_RIGHT = MAX_RIGHT / MAX98357

nets:
  VBAT_P: R1.1, R2.1, C1.+_or_1, C2.+_or_1, U1.14, F1.2, IP5310.B+
  BUTTON_N: R1.2, C3.+_or_1, U1.1, U1.2, SW1.1
  NOT_HOLD: R2.2, Q1.C, U1.5
  HOLD: R3.1, R15.1, D2.A, ESP32.GPIO18_proposed
  Q1_B: R3.2, R4.1, Q1.B
  GND: R4.2, R6.2, R9.2, R11.2, R13.2, R15.2, C1.-_or_2, C2.-_or_2, C3.-_or_2, C4.-_or_2, Q1.E, Q2.E, Q4.E, Q5.E, U1.7, U1.12, U1.13, SW1.2, PROTECT.P-_or_OUT-, RELAY.-, IP5310.B-, IP5310.USB-A_GND, IP5310.button_ground_pad, ESP32.GND, MAX_LEFT.GND, MAX_RIGHT.GND
  OR_NODE: R5.1, D1.K_band, D2.K_band
  Q2_B: R5.2, R6.1, Q2.B
  Q2_C: R7.1, Q2.C
  Q3_B: R7.2, R8.2, Q3.B
  5V_PRE: R8.1, Q3.E, RELAY.+, RELAY.COM, IP5310.USB-A_+5V
  RELAY_S: R9.1, Q3.C, RELAY.S
  START: R10.1, D1.A, U1.8
  Q4_B: R10.2, R11.1, Q4.B
  PRESSED: R12.1, U1.3, U1.4
  Q5_B: R12.2, R13.1, Q5.B
  3V3_RADIO: R14.1, ESP32.3V3
  BUTTON_READ: R14.2, Q5.C, ESP32.GPIO7
  5V_RADIO: C4.+_or_1, RELAY.NO, ESP32.5V/VIN, MAX_LEFT.VIN, MAX_RIGHT.VIN
  KEY: Q4.C, IP5310.button_KEY_pad
  START_N: U1.6, U1.9, U1.10
  CELL_PLUS: PROTECT.B+, CELL1.+, CELL2.+
  CELL_MINUS: PROTECT.B-, CELL1.-, CELL2.-
  PACK_PLUS: PROTECT.P+_or_OUT+, F1.1

custom parts:
  R1 / 100k: Terminal wiring representation. Pad placement and scale are illustrative. No PCB footprint or simulation model. See relay-power/README.md for prototype checks.
  R2 / 100k: Terminal wiring representation. Pad placement and scale are illustrative. No PCB footprint or simulation model. See relay-power/README.md for prototype checks.
  R3 / 10k: Terminal wiring representation. Pad placement and scale are illustrative. No PCB footprint or simulation model. See relay-power/README.md for prototype checks.
  R4 / 100k: Terminal wiring representation. Pad placement and scale are illustrative. No PCB footprint or simulation model. See relay-power/README.md for prototype checks.
  R5 / 1k: Terminal wiring representation. Pad placement and scale are illustrative. No PCB footprint or simulation model. See relay-power/README.md for prototype checks.
  R6 / 100k: Terminal wiring representation. Pad placement and scale are illustrative. No PCB footprint or simulation model. See relay-power/README.md for prototype checks.
  R7 / 1k: Terminal wiring representation. Pad placement and scale are illustrative. No PCB footprint or simulation model. See relay-power/README.md for prototype checks.
  R8 / 47k: Terminal wiring representation. Pad placement and scale are illustrative. No PCB footprint or simulation model. See relay-power/README.md for prototype checks.
  R9 / 10k: Terminal wiring representation. Pad placement and scale are illustrative. No PCB footprint or simulation model. See relay-power/README.md for prototype checks.
  R10 / 22k: Terminal wiring representation. Pad placement and scale are illustrative. No PCB footprint or simulation model. See relay-power/README.md for prototype checks.
  R11 / 100k: Terminal wiring representation. Pad placement and scale are illustrative. No PCB footprint or simulation model. See relay-power/README.md for prototype checks.
  R12 / 47k: Terminal wiring representation. Pad placement and scale are illustrative. No PCB footprint or simulation model. See relay-power/README.md for prototype checks.
  R13 / 100k: Terminal wiring representation. Pad placement and scale are illustrative. No PCB footprint or simulation model. See relay-power/README.md for prototype checks.
  R14 / 10k: Terminal wiring representation. Pad placement and scale are illustrative. No PCB footprint or simulation model. See relay-power/README.md for prototype checks.
  R15 / 100k: Terminal wiring representation. Pad placement and scale are illustrative. No PCB footprint or simulation model. See relay-power/README.md for prototype checks.
  C1 / 100nF: Terminal wiring representation. Pad placement and scale are illustrative. No PCB footprint or simulation model. See relay-power/README.md for prototype checks.
  C2 / 1uF: Terminal wiring representation. Pad placement and scale are illustrative. No PCB footprint or simulation model. See relay-power/README.md for prototype checks.
  C3 / 10nF: Terminal wiring representation. Pad placement and scale are illustrative. No PCB footprint or simulation model. See relay-power/README.md for prototype checks.
  C4 / 470uF 16V: Terminal wiring representation. Pad placement and scale are illustrative. No PCB footprint or simulation model. See relay-power/README.md for prototype checks.
  D1 / 1N4148: Terminal wiring representation. Pad placement and scale are illustrative. No PCB footprint or simulation model. See relay-power/README.md for prototype checks.
  D2 / 1N4148: Terminal wiring representation. Pad placement and scale are illustrative. No PCB footprint or simulation model. See relay-power/README.md for prototype checks.
  Q1 / 2N3904: Terminal wiring representation. Pad placement and scale are illustrative. No PCB footprint or simulation model. See relay-power/README.md for prototype checks.
  Q2 / 2N3904: Terminal wiring representation. Pad placement and scale are illustrative. No PCB footprint or simulation model. See relay-power/README.md for prototype checks.
  Q3 / 2N3906: Terminal wiring representation. Pad placement and scale are illustrative. No PCB footprint or simulation model. See relay-power/README.md for prototype checks.
  Q4 / 2N3904: Terminal wiring representation. Pad placement and scale are illustrative. No PCB footprint or simulation model. See relay-power/README.md for prototype checks.
  Q5 / 2N3904: Terminal wiring representation. Pad placement and scale are illustrative. No PCB footprint or simulation model. See relay-power/README.md for prototype checks.
  U1 / SN74HC132N: Terminal wiring representation. Pad placement and scale are illustrative. No PCB footprint or simulation model. See relay-power/README.md for prototype checks.
  SW1 / encoder momentary: Terminal wiring representation. Pad placement and scale are illustrative. No PCB footprint or simulation model. See relay-power/README.md for prototype checks.
  PROTECT / 1S >=6A; exact board to verify: Terminal wiring representation. Pad placement and scale are illustrative. No PCB footprint or simulation model. See relay-power/README.md for prototype checks.
  F1 / 5A time-delay provisional: Terminal wiring representation. Pad placement and scale are illustrative. No PCB footprint or simulation model. See relay-power/README.md for prototype checks.
  CELL1 / matched 18650: Terminal wiring representation. Pad placement and scale are illustrative. No PCB footprint or simulation model. See relay-power/README.md for prototype checks.
  CELL2 / matched 18650: Terminal wiring representation. Pad placement and scale are illustrative. No PCB footprint or simulation model. See relay-power/README.md for prototype checks.
  RELAY / existing Songle module: Terminal wiring representation. Pad placement and scale are illustrative. No PCB footprint or simulation model. See relay-power/README.md for prototype checks.
  IP5310 / USB-C + USB-A: Terminal wiring representation. Pad placement and scale are illustrative. No PCB footprint or simulation model. See relay-power/README.md for prototype checks.
  ESP32 / existing dev board: Terminal wiring representation. Pad placement and scale are illustrative. No PCB footprint or simulation model. See relay-power/README.md for prototype checks.
  MAX_LEFT / MAX98357: Terminal wiring representation. Pad placement and scale are illustrative. No PCB footprint or simulation model. See relay-power/README.md for prototype checks.
  MAX_RIGHT / MAX98357: Terminal wiring representation. Pad placement and scale are illustrative. No PCB footprint or simulation model. See relay-power/README.md for prototype checks.
